// Logisim project registrador8bits.circ as structural Verilog: 7 circuits, main circuit main
module main (
  input  clk,
  input  enable,
  input  reset,
  input  d0,
  input  d0_2,
  input  d0_3,
  input  d0_4,
  input  d0_5,
  input  d0_6,
  input  d0_7,
  input  d0_8,
  output out_12,
  output out_13,
  output out_14,
  output out_15,
  output out_16,
  output out_17,
  output out_18,
  output out_19
);

  wire and_1_out, and_2_out, and_3_out, and_4_out, and_5_out, and_6_out, and_7_out, and_8_out, and_9_out,
       not_1_out;

  not not_1 (not_1_out, reset);
  and and_1 (and_1_out, not_1_out, d0);
  and and_2 (and_2_out, not_1_out, d0_2);
  and and_3 (and_3_out, not_1_out, d0_3);
  and and_4 (and_4_out, not_1_out, d0_4);
  and and_5 (and_5_out, not_1_out, d0_5);
  and and_6 (and_6_out, not_1_out, d0_6);
  and and_7 (and_7_out, not_1_out, d0_7);
  and and_8 (and_8_out, not_1_out, d0_8);
  and and_9 (and_9_out, clk, enable);
  registrador8bits registrador8bits_1 (
    .in_1(and_9_out), .in_2(and_1_out), .in_3(and_2_out), .in_4(and_3_out), .in_5(and_4_out),
    .in_6(and_5_out), .in_7(and_6_out), .in_8(and_7_out), .in_9(and_8_out), .out_10(out_12), .out_11(out_13),
    .out_12(out_14), .out_13(out_15), .out_14(out_16), .out_15(out_17), .out_16(out_18), .out_17(out_19));
endmodule

module latchsr (
  input  r,
  input  s,
  output q
);

  wire not_2_out, or_1_out, or_2_out;

  or or_1 (or_1_out, r, not_2_out);
  or or_2 (or_2_out, q, s);
  not not_1 (q, or_1_out);
  not not_2 (not_2_out, or_2_out);
endmodule

module latchd (
  input  clk,
  input  d,
  output q
);

  wire and_1_out, and_2_out, not_1_out;

  not not_1 (not_1_out, d);
  and and_1 (and_1_out, clk, not_1_out);
  and and_2 (and_2_out, clk, d);
  latchsr latchsr_1 (.r(and_1_out), .s(and_2_out), .q(q));
endmodule

module flipflop (
  input  clk,
  input  d,
  output q
);

  wire latchd_1_q, not_1_out;

  not not_1 (not_1_out, clk);
  latchd latchd_1 (.clk(not_1_out), .d(d), .q(latchd_1_q));
  latchd latchd_2 (.clk(clk), .d(latchd_1_q), .q(q));
endmodule

module registrador2bits (
  input  clk,
  input  d0,
  input  d1,
  output out_4,
  output out_5
);

  flipflop flipflop_1 (.clk(clk), .d(d0), .q(out_4));
  flipflop flipflop_2 (.clk(clk), .d(d1), .q(out_5));
endmodule

module registrador4bits (
  input  clk,
  input  d0,
  input  d1,
  input  d2,
  input  d3,
  output q0,
  output q1,
  output q2,
  output q3
);

  registrador2bits registrador2bits_1 (.clk(clk), .d0(d0), .d1(d1), .out_4(q0), .out_5(q1));
  registrador2bits registrador2bits_2 (.clk(clk), .d0(d2), .d1(d3), .out_4(q2), .out_5(q3));
endmodule

module registrador8bits (
  input  in_1,
  input  in_2,
  input  in_3,
  input  in_4,
  input  in_5,
  input  in_6,
  input  in_7,
  input  in_8,
  input  in_9,
  output out_10,
  output out_11,
  output out_12,
  output out_13,
  output out_14,
  output out_15,
  output out_16,
  output out_17
);

  registrador4bits registrador4bits_1 (
    .clk(in_1), .d0(in_2), .d1(in_3), .d2(in_4), .d3(in_5), .q0(out_10), .q1(out_11), .q2(out_12), .q3(out_13));
  registrador4bits registrador4bits_2 (
    .clk(in_1), .d0(in_6), .d1(in_7), .d2(in_8), .d3(in_9), .q0(out_14), .q1(out_15), .q2(out_16), .q3(out_17));
endmodule
