// Logisim project somaregistra8bits.circ as structural Verilog: 5 circuits, main circuit main
module main (
  input  clk,
  input  enable,
  input  reset,
  input  sumsub,
  input  a0,
  input  b0,
  input  a1,
  input  b1,
  input  a2,
  input  b2,
  input  a3,
  input  b3,
  input  a4,
  input  b4,
  input  a5,
  input  enable2,
  input  b5,
  input  reset2,
  input  a6,
  input  b6,
  input  a7,
  input  b7,
  output out_23,
  output out_24,
  output out_25,
  output out_26,
  output out_27,
  output out_28,
  output out_29,
  output out_30,
  output out_31,
  output out_32,
  output out_33,
  output out_34,
  output out_35,
  output out_36,
  output out_37,
  output out_38,
  output out_39
);

  wire Somador8bits_out_18, Somador8bits_out_19, Somador8bits_out_20, Somador8bits_out_21,
       Somador8bits_out_22, Somador8bits_out_23, Somador8bits_out_24, Somador8bits_out_25;

  fulladder8bits Somador8bits (
    .sumsub(sumsub), .in_2(a0), .in_3(b0), .in_4(a1), .in_5(b1), .a0(a2), .b0(b2), .in_8(a3), .in_9(b3),
    .in_10(a4), .in_11(b4), .in_12(a5), .in_13(b5), .in_14(a6), .in_15(b6), .in_16(a7), .in_17(b7),
    .out_18(Somador8bits_out_18), .out_19(Somador8bits_out_19), .out_20(Somador8bits_out_20),
    .out_21(Somador8bits_out_21), .out_22(Somador8bits_out_22), .out_23(Somador8bits_out_23),
    .out_24(Somador8bits_out_24), .out_25(Somador8bits_out_25), .out_26(out_39));
  registrador8bits_main Registrador8bits (
    .clk(clk), .enable(enable), .reset(reset), .d0(Somador8bits_out_18), .d0_2(Somador8bits_out_19),
    .d0_3(Somador8bits_out_20), .d0_4(Somador8bits_out_21), .d0_5(Somador8bits_out_22),
    .d0_6(Somador8bits_out_23), .d0_7(Somador8bits_out_24), .d0_8(Somador8bits_out_25), .out_12(out_23),
    .out_13(out_24), .out_14(out_25), .out_15(out_26), .out_16(out_27), .out_17(out_28), .out_18(out_29),
    .out_19(out_30));
  registrador8bits_main Registrador8bits2 (
    .clk(clk), .enable(enable2), .reset(reset2), .d0(Somador8bits_out_18), .d0_2(Somador8bits_out_19),
    .d0_3(Somador8bits_out_20), .d0_4(Somador8bits_out_21), .d0_5(Somador8bits_out_22),
    .d0_6(Somador8bits_out_23), .d0_7(Somador8bits_out_24), .d0_8(Somador8bits_out_25), .out_12(out_31),
    .out_13(out_32), .out_14(out_33), .out_15(out_34), .out_16(out_35), .out_17(out_36), .out_18(out_37),
    .out_19(out_38));
endmodule

module \xor  (
  input  in_1,
  input  in_2,
  output out_3
);

  wire and_1_out, and_2_out, not_1_out, not_2_out;

  not not_1 (not_1_out, in_1);
  not not_2 (not_2_out, in_2);
  and and_1 (and_1_out, not_1_out, in_2);
  and and_2 (and_2_out, in_1, not_2_out);
  or or_1 (out_3, and_1_out, and_2_out);
endmodule

module fulladder (
  input  ci,
  input  a,
  input  b,
  output So,
  output co
);

  wire and_1_out, and_2_out, xor_1_out_3;

  \xor  xor_1 (.in_1(a), .in_2(b), .out_3(xor_1_out_3));
  and and_1 (and_1_out, ci, xor_1_out_3);
  and and_2 (and_2_out, a, b);
  \xor  xor_2 (.in_1(ci), .in_2(xor_1_out_3), .out_3(So));
  or or_1 (co, and_1_out, and_2_out);
endmodule

module fulladder4bits (
  input  sumsub,
  input  a0,
  input  b0,
  input  a1,
  input  b1,
  input  a2,
  input  b2,
  input  a3,
  input  b3,
  output s1,
  output s2,
  output s3,
  output s4,
  output co
);

  wire fulladder_1_co, fulladder_2_co, fulladder_3_co, xor_1_out_3, xor_2_out_3, xor_3_out_3, xor_4_out_3;

  \xor  xor_1 (.in_1(b0), .in_2(sumsub), .out_3(xor_1_out_3));
  \xor  xor_2 (.in_1(b1), .in_2(sumsub), .out_3(xor_2_out_3));
  \xor  xor_3 (.in_1(b2), .in_2(sumsub), .out_3(xor_3_out_3));
  \xor  xor_4 (.in_1(b3), .in_2(sumsub), .out_3(xor_4_out_3));
  fulladder fulladder_1 (.ci(sumsub), .a(a0), .b(xor_1_out_3), .So(s1), .co(fulladder_1_co));
  fulladder fulladder_2 (.ci(fulladder_1_co), .a(a1), .b(xor_2_out_3), .So(s2), .co(fulladder_2_co));
  fulladder fulladder_3 (.ci(fulladder_2_co), .a(a2), .b(xor_3_out_3), .So(s3), .co(fulladder_3_co));
  fulladder fulladder_4 (.ci(fulladder_3_co), .a(a3), .b(xor_4_out_3), .So(s4), .co(co));
endmodule

module fulladder8bits (
  input  sumsub,
  input  in_2,
  input  in_3,
  input  in_4,
  input  in_5,
  input  a0,
  input  b0,
  input  in_8,
  input  in_9,
  input  in_10,
  input  in_11,
  input  in_12,
  input  in_13,
  input  in_14,
  input  in_15,
  input  in_16,
  input  in_17,
  output out_18,
  output out_19,
  output out_20,
  output out_21,
  output out_22,
  output out_23,
  output out_24,
  output out_25,
  output out_26
);

  wire fulladder4bits_1_co;

  fulladder4bits fulladder4bits_1 (
    .sumsub(sumsub), .a0(in_2), .b0(in_3), .a1(in_4), .b1(in_5), .a2(a0), .b2(b0), .a3(in_8), .b3(in_9),
    .s1(out_18), .s2(out_19), .s3(out_20), .s4(out_21), .co(fulladder4bits_1_co));
  fulladder4bits fulladder4bits_2 (
    .sumsub(fulladder4bits_1_co), .a0(in_10), .b0(in_11), .a1(in_12), .b1(in_13), .a2(in_14), .b2(in_15),
    .a3(in_16), .b3(in_17), .s1(out_22), .s2(out_23), .s3(out_24), .s4(out_25), .co(out_26));
endmodule
